// Logisim project projet.circ as structural Verilog
module main (
);

  wire button_1_out, button_2_out, button_3_out, button_4_out, clock_1_out, dipswitch_1_sw1, dipswitch_1_sw2,
       dipswitch_1_sw3, dipswitch_1_sw4, dipswitch_1_sw5, dipswitch_1_sw6, dipswitch_1_sw7, dipswitch_1_sw8,
       dipswitch_1_sw9, dipswitch_1_sw10, memory_time_2_carry, memory_time_3_carry, memory_time_4_carry,
       output_logic_1_a, output_logic_1_b, output_logic_1_c, output_logic_1_d, output_logic_1_e,
       output_logic_1_f, output_logic_1_g, output_logic_1_p, output_logic_2_a, output_logic_2_b,
       output_logic_2_c, output_logic_2_d, output_logic_2_e, output_logic_2_f, output_logic_2_g,
       output_logic_2_p, output_logic_3_a, output_logic_3_b, output_logic_3_c, output_logic_3_d,
       output_logic_3_e, output_logic_3_f, output_logic_3_g, output_logic_3_p, output_logic_4_a,
       output_logic_4_b, output_logic_4_c, output_logic_4_d, output_logic_4_e, output_logic_4_f,
       output_logic_4_g, output_logic_4_p, output_logic_5_a, output_logic_5_b, output_logic_5_c,
       output_logic_5_d, output_logic_5_e, output_logic_5_f, output_logic_5_g, output_logic_5_p,
       output_logic_6_a, output_logic_6_b, output_logic_6_c, output_logic_6_d, output_logic_6_e,
       output_logic_6_f, output_logic_6_g, output_logic_6_p;

  DipSwitch #(.number(10)) dipswitch_1 (
    .sw1(dipswitch_1_sw1), .sw2(dipswitch_1_sw2), .sw3(dipswitch_1_sw3), .sw4(dipswitch_1_sw4),
    .sw5(dipswitch_1_sw5), .sw6(dipswitch_1_sw6), .sw7(dipswitch_1_sw7), .sw8(dipswitch_1_sw8),
    .sw9(dipswitch_1_sw9), .sw10(dipswitch_1_sw10));
  Button button_1 (.out(button_1_out));
  Button button_2 (.out(button_2_out));
  Button button_3 (.out(button_3_out));
  Clock clock_1 (.out(clock_1_out));
  Button button_4 (.out(button_4_out));
  transition_logic transition_logic_1 (
    .B_1(button_1_out), .B_0(button_2_out), .DS_9(dipswitch_1_sw10), .DS_8(dipswitch_1_sw9),
    .DS_7(dipswitch_1_sw8), .DS_6(dipswitch_1_sw7), .DS_5(dipswitch_1_sw6), .DS_4(dipswitch_1_sw5),
    .DS_3(dipswitch_1_sw4), .DS_2(dipswitch_1_sw3), .DS_1(dipswitch_1_sw2), .DS_0(dipswitch_1_sw1));  // open: f
  memory_time memory_time_1 (
    .inc(memory_time_2_carry), .clock(clock_1_out), .reset(button_4_out));  // open: carry, t_5, t_4, t_3, t_2, t_1, t_0
  memory_time memory_time_2 (
    .inc(memory_time_3_carry), .clock(clock_1_out), .reset(button_4_out), .carry(memory_time_2_carry));  // open: t_5, t_4, t_3, t_2, t_1, t_0
  memory_time memory_time_3 (
    .inc(memory_time_4_carry), .clock(clock_1_out), .reset(button_4_out), .carry(memory_time_3_carry));  // open: t_5, t_4, t_3, t_2, t_1, t_0
  memory_time memory_time_4 (
    .inc(button_3_out), .clock(clock_1_out), .reset(button_4_out), .carry(memory_time_4_carry));  // open: t_5, t_4, t_3, t_2, t_1, t_0
  output_logic output_logic_1 (
    .a(output_logic_1_a), .b(output_logic_1_b), .c(output_logic_1_c), .d(output_logic_1_d),
    .e(output_logic_1_e), .f(output_logic_1_f), .g(output_logic_1_g), .p(output_logic_1_p));  // open: I_5, I_4, I_3, I_2, I_1, I_0
  output_logic output_logic_2 (
    .a(output_logic_2_a), .b(output_logic_2_b), .c(output_logic_2_c), .d(output_logic_2_d),
    .e(output_logic_2_e), .f(output_logic_2_f), .g(output_logic_2_g), .p(output_logic_2_p));  // open: I_5, I_4, I_3, I_2, I_1, I_0
  output_logic output_logic_3 (
    .a(output_logic_3_a), .b(output_logic_3_b), .c(output_logic_3_c), .d(output_logic_3_d),
    .e(output_logic_3_e), .f(output_logic_3_f), .g(output_logic_3_g), .p(output_logic_3_p));  // open: I_5, I_4, I_3, I_2, I_1, I_0
  output_logic output_logic_4 (
    .a(output_logic_4_a), .b(output_logic_4_b), .c(output_logic_4_c), .d(output_logic_4_d),
    .e(output_logic_4_e), .f(output_logic_4_f), .g(output_logic_4_g), .p(output_logic_4_p));  // open: I_5, I_4, I_3, I_2, I_1, I_0
  output_logic output_logic_5 (
    .a(output_logic_5_a), .b(output_logic_5_b), .c(output_logic_5_c), .d(output_logic_5_d),
    .e(output_logic_5_e), .f(output_logic_5_f), .g(output_logic_5_g), .p(output_logic_5_p));  // open: I_5, I_4, I_3, I_2, I_1, I_0
  output_logic output_logic_6 (
    .a(output_logic_6_a), .b(output_logic_6_b), .c(output_logic_6_c), .d(output_logic_6_d),
    .e(output_logic_6_e), .f(output_logic_6_f), .g(output_logic_6_g), .p(output_logic_6_p));  // open: I_5, I_4, I_3, I_2, I_1, I_0
  _7_Segment_Display u_7_segment_display_1 (
    .g(output_logic_1_f), .f(output_logic_1_g), .a(output_logic_1_a), .b(output_logic_1_b),
    .e(output_logic_1_e), .d(output_logic_1_d), .c(output_logic_1_c), .dp(output_logic_1_p));
  _7_Segment_Display u_7_segment_display_2 (
    .g(output_logic_2_f), .f(output_logic_2_g), .a(output_logic_2_a), .b(output_logic_2_b),
    .e(output_logic_2_e), .d(output_logic_2_d), .c(output_logic_2_c), .dp(output_logic_2_p));
  _7_Segment_Display u_7_segment_display_3 (
    .g(output_logic_3_f), .f(output_logic_3_g), .a(output_logic_3_a), .b(output_logic_3_b),
    .e(output_logic_3_e), .d(output_logic_3_d), .c(output_logic_3_c), .dp(output_logic_3_p));
  _7_Segment_Display u_7_segment_display_4 (
    .g(output_logic_4_f), .f(output_logic_4_g), .a(output_logic_4_a), .b(output_logic_4_b),
    .e(output_logic_4_e), .d(output_logic_4_d), .c(output_logic_4_c), .dp(output_logic_4_p));
  _7_Segment_Display u_7_segment_display_5 (
    .g(output_logic_5_f), .f(output_logic_5_g), .a(output_logic_5_a), .b(output_logic_5_b),
    .e(output_logic_5_e), .d(output_logic_5_d), .c(output_logic_5_c), .dp(output_logic_5_p));
  _7_Segment_Display u_7_segment_display_6 (
    .g(output_logic_6_f), .f(output_logic_6_g), .a(output_logic_6_a), .b(output_logic_6_b),
    .e(output_logic_6_e), .d(output_logic_6_d), .c(output_logic_6_c), .dp(output_logic_6_p));
endmodule

module output_logic (
  input  I_5,
  input  I_4,
  input  I_3,
  input  I_2,
  input  I_1,
  input  I_0,
  output a,
  output b,
  output c,
  output d,
  output e,
  output f,
  output g,
  output p
);

  wire and_1_out, and_2_out, and_3_out, and_4_out, and_5_out, and_6_out, and_7_out, and_8_out, and_9_out,
       and_10_out, and_11_out, and_12_out, and_13_out, and_14_out, and_15_out, and_16_out, not_1_out,
       not_2_out, not_3_out, not_4_out, not_5_out, not_6_out, not_7_out, not_8_out, not_9_out, not_10_out,
       not_11_out, not_12_out, not_13_out, not_14_out, not_15_out, not_16_out, not_17_out, not_18_out,
       not_19_out, not_20_out, not_21_out;

  not not_1 (not_1_out, I_2);
  not not_2 (not_2_out, I_0);
  not not_3 (not_3_out, I_1);
  not not_4 (not_4_out, I_0);
  not not_5 (not_5_out, I_1);
  not not_6 (not_6_out, I_2);
  not not_7 (not_7_out, I_0);
  not not_8 (not_8_out, I_2);
  not not_9 (not_9_out, I_0);
  not not_10 (not_10_out, I_1);
  not not_11 (not_11_out, I_2);
  not not_12 (not_12_out, I_0);
  not not_13 (not_13_out, I_0);
  not not_14 (not_14_out, I_1);
  not not_15 (not_15_out, I_0);
  not not_16 (not_16_out, I_1);
  not not_17 (not_17_out, I_0);
  not not_18 (not_18_out, I_2);
  not not_19 (not_19_out, I_1);
  not not_20 (not_20_out, I_0);
  and and_1 (and_1_out, not_1_out, not_2_out);
  and and_2 (and_2_out, I_2, I_0);
  not not_21 (not_21_out, I_2);
  or or_1 (b, not_21_out, and_3_out, and_4_out);
  and and_3 (and_3_out, not_3_out, not_4_out);
  and and_4 (and_4_out, I_1, I_0);
  or or_2 (c, not_5_out, I_0, I_2);
  and and_5 (and_5_out, not_6_out, not_7_out);
  and and_6 (and_6_out, not_8_out, I_1);
  and and_7 (and_7_out, I_1, not_9_out);
  and and_8 (and_8_out, I_2, not_10_out, I_0);
  and and_9 (and_9_out, not_11_out, not_12_out);
  or or_3 (e, and_9_out, and_10_out);
  and and_10 (and_10_out, I_1, not_13_out);
  and and_11 (and_11_out, not_14_out, not_15_out);
  and and_12 (and_12_out, I_2, not_16_out);
  and and_13 (and_13_out, I_2, not_17_out);
  and and_14 (and_14_out, not_18_out, I_1);
  and and_15 (and_15_out, I_2, not_19_out);
  and and_16 (and_16_out, I_2, not_20_out);
  or or_4 (a, and_1_out, I_1, and_2_out, I_3);
  or or_5 (d, and_5_out, and_6_out, and_7_out, and_8_out, I_3);
  or or_6 (f, and_11_out, and_12_out, and_13_out, I_3);
  or or_7 (g, and_14_out, and_15_out, and_16_out, I_3);

  assign p = 1'b0;
endmodule

module transition_logic (
  input  B_1,
  input  B_0,
  input  DS_9,
  input  DS_8,
  input  DS_7,
  input  DS_6,
  input  DS_5,
  input  DS_4,
  input  DS_3,
  input  DS_2,
  input  DS_1,
  input  DS_0,
  input  f
);
endmodule

module memory_time (
  input  inc,
  input  clock,
  input  reset,
  output carry,
  output t_5,
  output t_4,
  output t_3,
  output t_2,
  output t_1,
  output t_0
);

  wire inc_6bits_1_c_out, inc_6bits_1_o_0, inc_6bits_1_o_1, inc_6bits_1_o_2, inc_6bits_1_o_3,
       inc_6bits_1_o_4, inc_6bits_1_o_5;

  inc_6bits inc_6bits_1 (
    .I_5(t_5), .I_4(t_4), .I_3(t_3), .I_2(t_2), .I_1(t_1), .I_0(t_0), .c_in(inc), .c_out(inc_6bits_1_c_out),
    .O_5(inc_6bits_1_o_5), .O_4(inc_6bits_1_o_4), .O_3(inc_6bits_1_o_3), .O_2(inc_6bits_1_o_2),
    .O_1(inc_6bits_1_o_1), .O_0(inc_6bits_1_o_0));
  D_Flip_Flop d_ff_1 (.D(inc_6bits_1_c_out), .clk(clock), .Q(carry), .reset(reset));  // open: Qn, preset
  D_Flip_Flop d_ff_2 (.D(inc_6bits_1_o_5), .clk(clock), .Q(t_5), .reset(reset));  // open: Qn, preset
  D_Flip_Flop d_ff_3 (.D(inc_6bits_1_o_4), .clk(clock), .Q(t_4), .reset(reset));  // open: Qn, preset
  D_Flip_Flop d_ff_4 (.D(inc_6bits_1_o_3), .clk(clock), .Q(t_3), .reset(reset));  // open: Qn, preset
  D_Flip_Flop d_ff_5 (.D(inc_6bits_1_o_2), .clk(clock), .Q(t_2), .reset(reset));  // open: Qn, preset
  D_Flip_Flop d_ff_6 (.D(inc_6bits_1_o_1), .clk(clock), .Q(t_1), .reset(reset));  // open: Qn, preset
  D_Flip_Flop d_ff_7 (.D(inc_6bits_1_o_0), .clk(clock), .Q(t_0), .reset(reset));  // open: Qn, preset
endmodule

module inc_6bits (
  input  I_5,
  input  I_4,
  input  I_3,
  input  I_2,
  input  I_1,
  input  I_0,
  input  c_in,
  output c_out,
  output O_5,
  output O_4,
  output O_3,
  output O_2,
  output O_1,
  output O_0
);

  wire half_adder_2_ci, half_adder_3_ci, half_adder_4_ci, half_adder_5_ci, half_adder_6_ci;

  half_adder half_adder_1 (.ai(I_5), .bi(half_adder_2_ci), .si(O_5), .ci(c_out));
  half_adder half_adder_2 (.ai(I_4), .bi(half_adder_3_ci), .si(O_4), .ci(half_adder_2_ci));
  half_adder half_adder_3 (.ai(I_3), .bi(half_adder_4_ci), .si(O_3), .ci(half_adder_3_ci));
  half_adder half_adder_4 (.ai(I_2), .bi(half_adder_5_ci), .si(O_2), .ci(half_adder_4_ci));
  half_adder half_adder_5 (.ai(I_1), .bi(half_adder_6_ci), .si(O_1), .ci(half_adder_5_ci));
  half_adder half_adder_6 (.ai(I_0), .bi(c_in), .si(O_0), .ci(half_adder_6_ci));
endmodule

module half_adder (
  input  ai,
  input  bi,
  output si,
  output ci
);

  xor xor_1 (si, ai, bi);
  and and_1 (ci, ai, bi);
endmodule

module full_adder (
  input  ai,
  input  bi,
  input  ciminus1,
  output si,
  output ci
);

  wire and_4_out, nand_1_out, nand_2_out, nand_3_out, xor_1_out;

  xor xor_1 (xor_1_out, ai, bi);
  // AND_Gate and_1 has open pins: in0=ai, in1=bi, out=open
  nand nand_1 (nand_1_out, ai, bi);
  nand nand_2 (nand_2_out, ai, ciminus1);
  // AND_Gate and_2 has open pins: in0=ai, in1=ciminus1, out=open
  // AND_Gate and_3 has open pins: in0=bi, in1=ciminus1, out=open
  nand nand_3 (nand_3_out, bi, ciminus1);
  xor xor_2 (si, xor_1_out, ciminus1);
  and and_4 (and_4_out, nand_1_out, nand_2_out);
  nand nand_4 (ci, and_4_out, nand_3_out);
endmodule
